# Fritzing sketch Demo 6 Schematic (saved by Fritzing 0.9.2b)
breadboards: 1

parts:
  Part1 = Arduino Uno (Rev3) - ICSP
  LED1 = smd LED [color="Red (633nm)" package="1206 [SMD]"]
  R1 = Resistor [tolerance=±5% resistance=220 package="0805 [SMD]"]
  YELLOW3 = Momentary Switch [package=ksa_sealed_tac_switch]

nets:
  N1: Part1.D12/MISO, LED1.anode
  N2: Part1.D3_PWM, YELLOW3.1
  N3: Part1.GND, R1.Pin_0, YELLOW3.3
  N4: LED1.cathode, R1.Pin_1
